# Fritzing sketch basement_monitor (saved by Fritzing 0.9.3b)
breadboards: 1

parts:
  Mod1 = Heltec WiFi Kit 32 [part_number=HTIT-WB32LA]
  DHT1 = DHT22 Humidity and Temperature Sensor
  R2 = Photocell (LDR) [package=THT]
  R4 = Resistor [tolerance=±5% resistance=10k package=THT]
  R5 = Resistor [tolerance=±5% resistance=220 package=THT]

nets:
  N1: Mod1.pin_7, DHT1.DATA, R4.Pin_0
  N2: Mod1.pin_15, Mod1.pin_18, Mod1.pin_19, DHT1.GND, R5.Pin_1
  N3: Mod1.pin_16, Mod1.pin_21, R2.pin_1
  N4: Mod1.pin_17, Mod1.pin_20, DHT1.VDD, R4.Pin_1
  N5: Mod1.pin_36, R2.pin_0, R5.Pin_0

custom parts:
  Heltec WiFi Kit 32: Heltec WiFi Kit 32 WiFi Kit 32 is a classic IoT dev-board designed & produced by Heltec Automation(TM). It’s a highly integrated product based on ESP32 + SX127x, it has Wi-Fi, BLE, LoRa functions, also Li-Po battery management system, 0.96″ OLED are also included. It’s the best choice for smart cities, smart farms, smart home, and IoT makers.
